// Logisim project part2c.circ as structural Verilog: 2 circuits, main circuit main
module main (
  input  i0,
  input  i1,
  input  i2,
  input  i3,
  input  i4,
  input  i5,
  input  i6,
  input  i7,
  input  L_H,
  input  En,
  input  [1:0] FunSel,
  output out0,
  output out1,
  output out2,
  output out3,
  output out4,
  output out5,
  output out6,
  output out7,
  output out8,
  output out9,
  output out10,
  output out11,
  output out12,
  output out13,
  output out14,
  output out15
);

  wire CLK_out;

  Hex_Digit_Display hex_digit_display_1 (.value({i7, i6, i5, i4}));  // open: dp
  Hex_Digit_Display hex_digit_display_2 (.value({i3, i2, i1, i0}));  // open: dp
  Clock CLK (.out(CLK_out));
  _2c u_2c_1 (
    .L_H(L_H), .CLK(CLK_out), .En(En), .FunSel(FunSel), .i0(i0), .i1(i1), .i2(i2), .i3(i3), .i4(i4), .i5(i5),
    .i6(i6), .i7(i7), .out0(out0), .out1(out1), .out2(out2), .out3(out3), .out4(out4), .out5(out5),
    .out6(out6), .out7(out7), .out8(out8), .out9(out9), .out10(out10), .out11(out11), .out12(out12),
    .out13(out13), .out14(out14), .out15(out15));
  Hex_Digit_Display hex_digit_display_3 (.value({out15, out14, out13, out12}));  // open: dp
  Hex_Digit_Display hex_digit_display_4 (.value({out11, out10, out9, out8}));  // open: dp
  Hex_Digit_Display hex_digit_display_5 (.value({out7, out6, out5, out4}));  // open: dp
  Hex_Digit_Display hex_digit_display_6 (.value({out3, out2, out1, out0}));  // open: dp
endmodule

module _2c (
  input  i0,
  input  i1,
  input  i2,
  input  i3,
  input  i4,
  input  i5,
  input  i6,
  input  i7,
  input  L_H,
  input  CLK,
  input  En,
  input  [1:0] FunSel,
  output out0,
  output out1,
  output out2,
  output out3,
  output out4,
  output out5,
  output out6,
  output out7,
  output out8,
  output out9,
  output out10,
  output out11,
  output out12,
  output out13,
  output out14,
  output out15
);

  wire multiplexer_1_out, multiplexer_2_out, multiplexer_3_out, multiplexer_4_out, multiplexer_6_out,
       multiplexer_7_out, multiplexer_8_out, multiplexer_9_out, multiplexer_10_out, multiplexer_11_out,
       multiplexer_12_out, multiplexer_13_out, multiplexer_14_out, multiplexer_15_out, multiplexer_16_out,
       multiplexer_17_out;
  wire [0:0] not_1_out;
  wire [1:0] multiplexer_5_out, not_3_out;
  wire [1:1] not_2_out;

  Hex_Digit_Display hex_digit_display_1 (.value({i7, i6, i5, i4}));  // open: dp
  Hex_Digit_Display hex_digit_display_2 (.value({i3, i2, i1, i0}));  // open: dp
  Multiplexer #(.enable("false")) multiplexer_1 (.in0(i0), .in1(out0), .out(multiplexer_1_out), .sel(L_H));
  not not_1 (not_1_out[0], FunSel[0]);
  not not_2 (not_2_out[1], FunSel[1]);
  Multiplexer #(.enable("false")) multiplexer_2 (.in0(i1), .in1(out1), .out(multiplexer_2_out), .sel(L_H));
  assign not_3_out = ~FunSel;  // NOT_Gate not_3, 2 bits wide
  Multiplexer #(.enable("false")) multiplexer_3 (.in0(i3), .in1(out3), .out(multiplexer_3_out), .sel(L_H));
  Multiplexer #(.enable("false")) multiplexer_4 (.in0(i2), .in1(out2), .out(multiplexer_4_out), .sel(L_H));
  Multiplexer #(.select(2), .width(2), .enable("false")) multiplexer_5 (
    .in0(FunSel), .in1(not_3_out), .in2({FunSel[1], not_1_out[0]}), .in3({not_2_out[1], FunSel[0]}),
    .out(multiplexer_5_out), .sel(FunSel));
  Multiplexer #(.enable("false")) multiplexer_6 (.in0(i5), .in1(out5), .out(multiplexer_6_out), .sel(L_H));
  Multiplexer #(.enable("false")) multiplexer_7 (.in0(i4), .in1(out4), .out(multiplexer_7_out), .sel(L_H));
  Multiplexer #(.enable("false")) multiplexer_8 (.in0(i6), .in1(out6), .out(multiplexer_8_out), .sel(L_H));
  Multiplexer #(.enable("false")) multiplexer_9 (.in0(out8), .in1(i0), .out(multiplexer_9_out), .sel(L_H));
  Multiplexer #(.enable("false")) multiplexer_10 (.in0(i7), .in1(out7), .out(multiplexer_10_out), .sel(L_H));
  Multiplexer #(.enable("false")) multiplexer_11 (.in0(out9), .in1(i1), .out(multiplexer_11_out), .sel(L_H));
  _16bit u_16bit_1 (
    .FunSel(multiplexer_5_out), .CLK(CLK), .Enable(En), .i0(multiplexer_1_out), .i1(multiplexer_2_out),
    .i2(multiplexer_4_out), .i3(multiplexer_3_out), .i4(multiplexer_7_out), .i5(multiplexer_6_out),
    .i6(multiplexer_8_out), .i7(multiplexer_10_out), .i8(multiplexer_9_out), .i9(multiplexer_11_out),
    .i10(multiplexer_12_out), .i11(multiplexer_13_out), .i12(multiplexer_15_out), .i13(multiplexer_14_out),
    .i14(multiplexer_16_out), .i15(multiplexer_17_out), .out0(out0), .out1(out1), .out2(out2), .out3(out3),
    .out4(out4), .out5(out5), .out6(out6), .out7(out7), .out8(out8), .out9(out9), .out10(out10),
    .out11(out11), .out12(out12), .out13(out13), .out14(out14), .out15(out15));
  Multiplexer #(.enable("false")) multiplexer_12 (.in0(out10), .in1(i2), .out(multiplexer_12_out), .sel(L_H));
  Multiplexer #(.enable("false")) multiplexer_13 (.in0(out11), .in1(i3), .out(multiplexer_13_out), .sel(L_H));
  Multiplexer #(.enable("false")) multiplexer_14 (.in0(out13), .in1(i5), .out(multiplexer_14_out), .sel(L_H));
  Multiplexer #(.enable("false")) multiplexer_15 (.in0(out12), .in1(i4), .out(multiplexer_15_out), .sel(L_H));
  Multiplexer #(.enable("false")) multiplexer_16 (.in0(out14), .in1(i6), .out(multiplexer_16_out), .sel(L_H));
  Multiplexer #(.enable("false")) multiplexer_17 (.in0(out15), .in1(i7), .out(multiplexer_17_out), .sel(L_H));
endmodule
