// Logisim project 16bit.circ as structural Verilog: 2 circuits, main circuit main
module main (
  input  [15:0] Input,
  input  [1:0] FunSel,
  input  Enable,
  output [15:0] Output
);

  wire CLK_out;

  Clock CLK (.out(CLK_out));
  Hex_Digit_Display hex_digit_display_1 (.value(Input[15:12]));  // open: dp
  Hex_Digit_Display hex_digit_display_2 (.value(Input[11:8]));  // open: dp
  Hex_Digit_Display hex_digit_display_3 (.value(Input[7:4]));  // open: dp
  _16bit u_16bit_1 (.FunSel(FunSel), .CLK(CLK_out), .Enable(Enable), .Input(Input), .Output(Output));
  Hex_Digit_Display hex_digit_display_4 (.value(Input[3:0]));  // open: dp
  Hex_Digit_Display hex_digit_display_5 (.value(Output[15:12]));  // open: dp
  Hex_Digit_Display hex_digit_display_6 (.value(Output[11:8]));  // open: dp
  Hex_Digit_Display hex_digit_display_7 (.value(Output[7:4]));  // open: dp
  Hex_Digit_Display hex_digit_display_8 (.value(Output[3:0]));  // open: dp
endmodule

module _16bit (
  input  [15:0] Input,
  input  [1:0] FunSel,
  input  CLK,
  input  Enable,
  output [15:0] Output
);

  wire adder_1_cout, adder_1_out, adder_2_cout, adder_2_out, adder_3_cout, adder_3_out, adder_4_cout,
       adder_4_out, adder_5_cout, adder_5_out, adder_6_cout, adder_6_out, adder_7_cout, adder_7_out,
       adder_8_cout, adder_8_out, adder_9_cout, adder_9_out, adder_10_cout, adder_10_out, adder_11_cout,
       adder_11_out, adder_12_cout, adder_12_out, adder_13_cout, adder_13_out, adder_14_cout, adder_14_out,
       adder_15_cout, adder_15_out, adder_16_out, multiplexer_1_out, multiplexer_2_out, multiplexer_3_out,
       multiplexer_4_out, multiplexer_5_out, multiplexer_6_out, multiplexer_7_out, multiplexer_8_out,
       multiplexer_9_out, multiplexer_10_out, multiplexer_11_out, multiplexer_12_out, multiplexer_13_out,
       multiplexer_14_out, multiplexer_15_out, multiplexer_16_out, not_1_out, not_2_out, subtractor_1_bout,
       subtractor_1_out, subtractor_2_bout, subtractor_2_out, subtractor_3_bout, subtractor_3_out,
       subtractor_4_bout, subtractor_4_out, subtractor_5_bout, subtractor_5_out, subtractor_6_bout,
       subtractor_6_out, subtractor_7_bout, subtractor_7_out, subtractor_8_bout, subtractor_8_out,
       subtractor_9_bout, subtractor_9_out, subtractor_10_bout, subtractor_10_out, subtractor_11_bout,
       subtractor_11_out, subtractor_12_bout, subtractor_12_out, subtractor_13_bout, subtractor_13_out,
       subtractor_14_bout, subtractor_14_out, subtractor_15_bout, subtractor_15_out, subtractor_16_out;

  Multiplexer #(.select(2), .enable("false")) multiplexer_1 (
    .in0(not_1_out), .in1(Input[0]), .in2(adder_1_out), .in3(subtractor_1_out), .out(multiplexer_1_out),
    .sel(FunSel));
  not not_1 (not_1_out, Enable);
  Adder #(.width(1)) adder_1 (.a(Output[0]), .b(Enable), .out(adder_1_out), .cout(adder_1_cout));  // open: cin
  Subtractor #(.width(1)) subtractor_1 (
    .a(Output[0]), .b(Enable), .out(subtractor_1_out), .bout(subtractor_1_bout));  // open: bin
  D_Flip_Flop d_ff_1 (.clk(CLK), .D(multiplexer_1_out), .Q(Output[0]), .en(Enable));  // open: Qn, preset, reset
  Multiplexer #(.select(2), .enable("false")) multiplexer_2 (
    .in0(not_1_out), .in1(Input[1]), .in2(adder_2_out), .in3(subtractor_2_out), .out(multiplexer_2_out),
    .sel(FunSel));
  D_Flip_Flop d_ff_2 (.clk(CLK), .D(multiplexer_2_out), .Q(Output[1]), .en(Enable));  // open: Qn, preset, reset
  Adder #(.width(1)) adder_2 (.a(Output[1]), .b(adder_1_cout), .out(adder_2_out), .cout(adder_2_cout));  // open: cin
  Subtractor #(.width(1)) subtractor_2 (
    .a(Output[1]), .b(subtractor_1_bout), .out(subtractor_2_out), .bout(subtractor_2_bout));  // open: bin
  Multiplexer #(.select(2), .enable("false")) multiplexer_3 (
    .in0(not_1_out), .in1(Input[2]), .in2(adder_3_out), .in3(subtractor_3_out), .out(multiplexer_3_out),
    .sel(FunSel));
  D_Flip_Flop d_ff_3 (.clk(CLK), .D(multiplexer_3_out), .Q(Output[2]), .en(Enable));  // open: Qn, preset, reset
  Adder #(.width(1)) adder_3 (.a(Output[2]), .b(adder_2_cout), .out(adder_3_out), .cout(adder_3_cout));  // open: cin
  Subtractor #(.width(1)) subtractor_3 (
    .a(Output[2]), .b(subtractor_2_bout), .out(subtractor_3_out), .bout(subtractor_3_bout));  // open: bin
  Multiplexer #(.select(2), .enable("false")) multiplexer_4 (
    .in0(not_1_out), .in1(Input[3]), .in2(adder_4_out), .in3(subtractor_4_out), .out(multiplexer_4_out),
    .sel(FunSel));
  D_Flip_Flop d_ff_4 (.clk(CLK), .D(multiplexer_4_out), .Q(Output[3]), .en(Enable));  // open: Qn, preset, reset
  Adder #(.width(1)) adder_4 (.a(Output[3]), .b(adder_3_cout), .out(adder_4_out), .cout(adder_4_cout));  // open: cin
  Subtractor #(.width(1)) subtractor_4 (
    .a(Output[3]), .b(subtractor_3_bout), .out(subtractor_4_out), .bout(subtractor_4_bout));  // open: bin
  Multiplexer #(.select(2), .enable("false")) multiplexer_5 (
    .in0(not_1_out), .in1(Input[4]), .in2(adder_5_out), .in3(subtractor_5_out), .out(multiplexer_5_out),
    .sel(FunSel));
  D_Flip_Flop d_ff_5 (.clk(CLK), .D(multiplexer_5_out), .Q(Output[4]), .en(Enable));  // open: Qn, preset, reset
  Adder #(.width(1)) adder_5 (.a(Output[4]), .b(adder_4_cout), .out(adder_5_out), .cout(adder_5_cout));  // open: cin
  Subtractor #(.width(1)) subtractor_5 (
    .a(Output[4]), .b(subtractor_4_bout), .out(subtractor_5_out), .bout(subtractor_5_bout));  // open: bin
  Multiplexer #(.select(2), .enable("false")) multiplexer_6 (
    .in0(not_1_out), .in1(Input[5]), .in2(adder_6_out), .in3(subtractor_6_out), .out(multiplexer_6_out),
    .sel(FunSel));
  D_Flip_Flop d_ff_6 (.clk(CLK), .D(multiplexer_6_out), .Q(Output[5]), .en(Enable));  // open: Qn, preset, reset
  Adder #(.width(1)) adder_6 (.a(Output[5]), .b(adder_5_cout), .out(adder_6_out), .cout(adder_6_cout));  // open: cin
  Subtractor #(.width(1)) subtractor_6 (
    .a(Output[5]), .b(subtractor_5_bout), .out(subtractor_6_out), .bout(subtractor_6_bout));  // open: bin
  Multiplexer #(.select(2), .enable("false")) multiplexer_7 (
    .in0(not_1_out), .in1(Input[6]), .in2(adder_7_out), .in3(subtractor_7_out), .out(multiplexer_7_out),
    .sel(FunSel));
  D_Flip_Flop d_ff_7 (.clk(CLK), .D(multiplexer_7_out), .Q(Output[6]), .en(Enable));  // open: Qn, preset, reset
  Adder #(.width(1)) adder_7 (.a(Output[6]), .b(adder_6_cout), .out(adder_7_out), .cout(adder_7_cout));  // open: cin
  Subtractor #(.width(1)) subtractor_7 (
    .a(Output[6]), .b(subtractor_6_bout), .out(subtractor_7_out), .bout(subtractor_7_bout));  // open: bin
  Multiplexer #(.select(2), .enable("false")) multiplexer_8 (
    .in0(not_1_out), .in1(Input[7]), .in2(adder_8_out), .in3(subtractor_8_out), .out(multiplexer_8_out),
    .sel(FunSel));
  D_Flip_Flop d_ff_8 (.clk(CLK), .D(multiplexer_8_out), .Q(Output[7]), .en(Enable));  // open: Qn, preset, reset
  Adder #(.width(1)) adder_8 (.a(Output[7]), .b(adder_7_cout), .out(adder_8_out), .cout(adder_8_cout));  // open: cin
  Subtractor #(.width(1)) subtractor_8 (
    .a(Output[7]), .b(subtractor_7_bout), .out(subtractor_8_out), .bout(subtractor_8_bout));  // open: bin
  not not_2 (not_2_out, Enable);
  Multiplexer #(.select(2), .enable("false")) multiplexer_9 (
    .in0(not_2_out), .in1(Input[8]), .in2(adder_9_out), .in3(subtractor_9_out), .out(multiplexer_9_out),
    .sel(FunSel));
  D_Flip_Flop d_ff_9 (.clk(CLK), .D(multiplexer_9_out), .Q(Output[8]), .en(Enable));  // open: Qn, preset, reset
  Adder #(.width(1)) adder_9 (.a(Output[8]), .b(adder_8_cout), .out(adder_9_out), .cout(adder_9_cout));  // open: cin
  Subtractor #(.width(1)) subtractor_9 (
    .a(Output[8]), .b(subtractor_8_bout), .out(subtractor_9_out), .bout(subtractor_9_bout));  // open: bin
  Multiplexer #(.select(2), .enable("false")) multiplexer_10 (
    .in0(not_2_out), .in1(Input[9]), .in2(adder_10_out), .in3(subtractor_10_out), .out(multiplexer_10_out),
    .sel(FunSel));
  D_Flip_Flop d_ff_10 (.clk(CLK), .D(multiplexer_10_out), .Q(Output[9]), .en(Enable));  // open: Qn, preset, reset
  Adder #(.width(1)) adder_10 (.a(Output[9]), .b(adder_9_cout), .out(adder_10_out), .cout(adder_10_cout));  // open: cin
  Subtractor #(.width(1)) subtractor_10 (
    .a(Output[9]), .b(subtractor_9_bout), .out(subtractor_10_out), .bout(subtractor_10_bout));  // open: bin
  Multiplexer #(.select(2), .enable("false")) multiplexer_11 (
    .in0(not_2_out), .in1(Input[10]), .in2(adder_11_out), .in3(subtractor_11_out), .out(multiplexer_11_out),
    .sel(FunSel));
  D_Flip_Flop d_ff_11 (.clk(CLK), .D(multiplexer_11_out), .Q(Output[10]), .en(Enable));  // open: Qn, preset, reset
  Adder #(.width(1)) adder_11 (
    .a(Output[10]), .b(adder_10_cout), .out(adder_11_out), .cout(adder_11_cout));  // open: cin
  Subtractor #(.width(1)) subtractor_11 (
    .a(Output[10]), .b(subtractor_10_bout), .out(subtractor_11_out), .bout(subtractor_11_bout));  // open: bin
  Multiplexer #(.select(2), .enable("false")) multiplexer_12 (
    .in0(not_2_out), .in1(Input[11]), .in2(adder_12_out), .in3(subtractor_12_out), .out(multiplexer_12_out),
    .sel(FunSel));
  D_Flip_Flop d_ff_12 (.clk(CLK), .D(multiplexer_12_out), .Q(Output[11]), .en(Enable));  // open: Qn, preset, reset
  Adder #(.width(1)) adder_12 (
    .a(Output[11]), .b(adder_11_cout), .out(adder_12_out), .cout(adder_12_cout));  // open: cin
  Subtractor #(.width(1)) subtractor_12 (
    .a(Output[11]), .b(subtractor_11_bout), .out(subtractor_12_out), .bout(subtractor_12_bout));  // open: bin
  Multiplexer #(.select(2), .enable("false")) multiplexer_13 (
    .in0(not_2_out), .in1(Input[12]), .in2(adder_13_out), .in3(subtractor_13_out), .out(multiplexer_13_out),
    .sel(FunSel));
  D_Flip_Flop d_ff_13 (.clk(CLK), .D(multiplexer_13_out), .Q(Output[12]), .en(Enable));  // open: Qn, preset, reset
  Adder #(.width(1)) adder_13 (
    .a(Output[12]), .b(adder_12_cout), .out(adder_13_out), .cout(adder_13_cout));  // open: cin
  Subtractor #(.width(1)) subtractor_13 (
    .a(Output[12]), .b(subtractor_12_bout), .out(subtractor_13_out), .bout(subtractor_13_bout));  // open: bin
  Multiplexer #(.select(2), .enable("false")) multiplexer_14 (
    .in0(not_2_out), .in1(Input[13]), .in2(adder_14_out), .in3(subtractor_14_out), .out(multiplexer_14_out),
    .sel(FunSel));
  D_Flip_Flop d_ff_14 (.clk(CLK), .D(multiplexer_14_out), .Q(Output[13]), .en(Enable));  // open: Qn, preset, reset
  Adder #(.width(1)) adder_14 (
    .a(Output[13]), .b(adder_13_cout), .out(adder_14_out), .cout(adder_14_cout));  // open: cin
  Subtractor #(.width(1)) subtractor_14 (
    .a(Output[13]), .b(subtractor_13_bout), .out(subtractor_14_out), .bout(subtractor_14_bout));  // open: bin
  Multiplexer #(.select(2), .enable("false")) multiplexer_15 (
    .in0(not_2_out), .in1(Input[14]), .in2(adder_15_out), .in3(subtractor_15_out), .out(multiplexer_15_out),
    .sel(FunSel));
  D_Flip_Flop d_ff_15 (.clk(CLK), .D(multiplexer_15_out), .Q(Output[14]), .en(Enable));  // open: Qn, preset, reset
  Adder #(.width(1)) adder_15 (
    .a(Output[14]), .b(adder_14_cout), .out(adder_15_out), .cout(adder_15_cout));  // open: cin
  Subtractor #(.width(1)) subtractor_15 (
    .a(Output[14]), .b(subtractor_14_bout), .out(subtractor_15_out), .bout(subtractor_15_bout));  // open: bin
  Multiplexer #(.select(2), .enable("false")) multiplexer_16 (
    .in0(not_2_out), .in1(Input[15]), .in2(adder_16_out), .in3(subtractor_16_out), .out(multiplexer_16_out),
    .sel(FunSel));
  D_Flip_Flop d_ff_16 (.clk(CLK), .D(multiplexer_16_out), .Q(Output[15]), .en(Enable));  // open: Qn, preset, reset
  Adder #(.width(1)) adder_16 (.a(Output[15]), .b(adder_15_cout), .out(adder_16_out));  // open: cin, cout
  Subtractor #(.width(1)) subtractor_16 (
    .a(Output[15]), .b(subtractor_15_bout), .out(subtractor_16_out));  // open: bin, bout
endmodule
