// Logisim project proj2part2.circ as structural Verilog: 1 circuit, main circuit main
module main (
  input  MuxCSel,
  input  [1:0] OutASel,
  input  [1:0] OutBSel,
  input  [3:0] RegSel,
  input  [3:0] FunSel,
  input  [1:0] FunSel_2,
  input  [1:0] MuxASel,
  input  [1:0] FunSel_3,
  input  [1:0] MuxBSel,
  input  [2:0] RegSel_2,
  input  [1:0] OutCsel,
  input  [1:0] OutDsel,
  input  L_H,
  input  En,
  input  [1:0] FunSel_4
);

  wire C_output, CLK_out;
  wire [3:0] ALU_outflag;
  wire [7:0] ALU_outalu, ARF_output_c, ARF_output_d, IR_output, IR_output_2, multiplexer_1_out,
       multiplexer_2_out, multiplexer_3_out, ram_1_data, RF_p7, RF_p8;

  Multiplexer #(.select(2), .width(8)) multiplexer_1 (
    .in0(IR_output), .in1(ram_1_data), .in2(ARF_output_c), .in3(ALU_outalu), .out(multiplexer_1_out),
    .sel(MuxASel));  // open: en
  Clock CLK (.out(CLK_out));
  _2c IR (.Input(ram_1_data), .L_H(L_H), .CLK(CLK_out), .En(En), .FunSel(FunSel_4), .Output({IR_output_2, IR_output}));
  // _2a RF: pin names not known; wires that end beside it: multiplexer_1_out, OutASel, OutBSel, RegSel, FunSel_2, CLK_out, RF_p7, RF_p8
  Multiplexer #(.width(8)) multiplexer_2 (
    .in0(multiplexer_1_out), .in1(RF_p7), .out(multiplexer_2_out), .sel(MuxCSel));  // open: en
  Multiplexer #(.select(2), .width(8)) multiplexer_3 (
    .in1(IR_output), .in2(ram_1_data), .in3(ALU_outalu), .out(multiplexer_3_out), .sel(MuxBSel));  // open: in0, en
  ALU ALU (
    .A(multiplexer_2_out), .B(RF_p8), .Carry_In(C_output), .FunSel(FunSel), .OutALU(ALU_outalu),
    .OutFlag(ALU_outflag));
  _2b ARF (
    .Inputs(multiplexer_3_out), .FunSel(FunSel_3), .CLK(CLK_out), .RegSel(RegSel_2), .OutCsel(OutCsel),
    .OutDsel(OutDsel), .Output_C(ARF_output_c), .Output_D(ARF_output_d));
  FR Z (.CLK(CLK_out), .Input(ALU_outflag[3]));  // open: Output
  FR C (.CLK(CLK_out), .Input(ALU_outflag[2]), .Output(C_output));
  FR N (.CLK(CLK_out), .Input(ALU_outflag[1]));  // open: Output
  FR O (.CLK(CLK_out), .Input(ALU_outflag[0]));  // open: Output
  RAM #(.bus("separate")) ram_1 (
    .addr(ARF_output_d), .din(ALU_outalu), .data(ram_1_data), .str(1'b1), .clk(CLK_out), .ld(1'b1));  // open: sel, clr

  // Notes on the sheet:
  //   A
  //   C
  //   B
endmodule
