// Logisim project proj1part2b.circ as structural Verilog: 2 circuits, main circuit main
module main (
  input  [7:0] Inputs,
  input  [1:0] FunSel,
  input  [1:0] OutCsel,
  input  [1:0] OutDsel,
  input  [2:0] RegSel,
  output [7:0] Output_C,
  output [7:0] Output_D
);

  wire CLK_out;

  Hex_Digit_Display hex_digit_display_1 (.value(Inputs[7:4]));  // open: dp
  Clock CLK (.out(CLK_out));
  Hex_Digit_Display hex_digit_display_2 (.value(Inputs[3:0]));  // open: dp
  _2b u_2b_1 (
    .Inputs(Inputs), .FunSel(FunSel), .CLK(CLK_out), .RegSel(RegSel), .OutCsel(OutCsel), .OutDsel(OutDsel),
    .Output_C(Output_C), .Output_D(Output_D));
  Hex_Digit_Display hex_digit_display_3 (.value(Output_C[7:4]));  // open: dp
  Hex_Digit_Display hex_digit_display_4 (.value(Output_C[3:0]));  // open: dp
  Hex_Digit_Display hex_digit_display_5 (.value(Output_D[7:4]));  // open: dp
  Hex_Digit_Display hex_digit_display_6 (.value(Output_D[3:0]));  // open: dp
endmodule

module _2b (
  input  [7:0] Inputs,
  input  [1:0] FunSel,
  input  CLK,
  input  [1:0] OutCsel,
  input  [1:0] OutDsel,
  input  [2:0] RegSel,
  output [7:0] Output_C,
  output [7:0] Output_D
);

  wire [7:0] AR_output, PC_output, SP_output;

  Hex_Digit_Display hex_digit_display_1 (.value(Inputs[7:4]));  // open: dp
  Hex_Digit_Display hex_digit_display_2 (.value(Inputs[3:0]));  // open: dp
  _8_bit PC (.Input(Inputs), .FunSel(FunSel), .CLK(CLK), .Enable(RegSel[0]), .Output(PC_output));
  _8_bit AR (.Input(Inputs), .FunSel(FunSel), .CLK(CLK), .Enable(RegSel[1]), .Output(AR_output));
  _8_bit SP (.Input(Inputs), .FunSel(FunSel), .CLK(CLK), .Enable(RegSel[2]), .Output(SP_output));
  Hex_Digit_Display hex_digit_display_3 (.value(Output_C[7:4]));  // open: dp
  Multiplexer #(.select(2), .width(8), .enable("false")) multiplexer_1 (
    .in0(PC_output), .in1(AR_output), .in2(SP_output), .in3(PC_output), .out(Output_C), .sel(OutCsel));
  Multiplexer #(.select(2), .width(8), .enable("false")) multiplexer_2 (
    .in0(PC_output), .in1(AR_output), .in2(SP_output), .in3(PC_output), .out(Output_D), .sel(OutDsel));
  Hex_Digit_Display hex_digit_display_4 (.value(Output_C[3:0]));  // open: dp
  Hex_Digit_Display hex_digit_display_5 (.value(Output_D[7:4]));  // open: dp
  Hex_Digit_Display hex_digit_display_6 (.value(Output_D[3:0]));  // open: dp
endmodule
