// Logisim project proj4.circ as structural Verilog: 8 circuits, main circuit main
module main (
);

  wire and_2_out, and_3_out, CLK_out, En, L_H, Load, MOP0, MOP1, MOP2, MOP3, MOP4, MOP5, MOP6, MOP7, MOP8,
       MOP9, MOP10, MOP11, MOP12, MOP13, MOP14, MOP15, MOP16, MOP17, MOP18, MOP19, MOP20, MOP21, MOP22,
       MOP23, MOP24, MOP25, MOP26, MOP27, MOP28, MOP29, MOP30, MOP31, MOP32, MOP33, MOP34, MOP35, MOP36,
       MOP37, MOP38, MOP39, MOP40, MOP41, MOP42, MOP43, MOP44, MOP45, MOP46, MOP47, MOP48, MOP49, MOP50,
       MOP51, MOP52, MOP53, MOP54, MOP55, MOP56, MOP57, MOP58, MOP59, MOP60, MOP61, MOP62, MOP63,
       multiplexer_1_out, MuxCSel, not_1_out, not_2_out, not_3_out, or_2_out, or_3_out, or_4_out, or_5_out,
       or_6_out, or_7_out, or_8_out, or_9_out, or_10_out, or_11_out, or_12_out, or_13_out, SBRLoad, Store, Z;
  wire [1:0] FunSelARF, FunSelIR, FunSelRF, MuxASel, MuxBSel, OutASel, OutBSel, OutConverter_2_output,
       OutConverter_3_output, OutConverter_output, OutCSel, OutDSel, rom_1_data_2, rom_1_data_3;
  wire [1:1] or_1_out;
  wire [2:0] ARFDecoder_output, RegSelARF;
  wire [3:0] FunSelALU, RegSelRF, RFDecoder_2_output, RFDecoder_output;
  wire [8:0] adder_1_out, CAR_output, MAP_output, multiplexer_2_out, rom_1_data, SBR_output;
  wire [15:0] IR;
  wire [18:13] rom_1_data_4;

  not not_1 (not_1_out, Z);
  and and_1 (SBRLoad, multiplexer_1_out, not_3_out, rom_1_data_2[0]);
  Multiplexer #(.select(2)) multiplexer_1 (
    .in0(1'b1), .in1(Z), .in2(not_1_out), .out(multiplexer_1_out), .sel(rom_1_data_3));  // open: in3, en
  and and_2 (and_2_out, multiplexer_1_out, not_2_out);
  not not_2 (not_2_out, rom_1_data_2[1]);
  not not_3 (not_3_out, rom_1_data_2[1]);
  and and_3 (and_3_out, rom_1_data_2[0], rom_1_data_2[1]);
  or or_1 (or_1_out[1], and_2_out, and_3_out);
  MAP MAP (.IR(IR), .Output(MAP_output));
  Multiplexer #(.select(2), .width(9)) multiplexer_2 (
    .in0(adder_1_out), .in1(SBR_output), .in2(rom_1_data), .in3(MAP_output), .out(multiplexer_2_out),
    .sel({or_1_out[1], rom_1_data_2[1]}));  // open: en
  CAR CAR (.CLK(CLK_out), .Input(multiplexer_2_out), .Output(CAR_output));
  ROM #(.addrWidth(9), .dataWidth(19)) rom_1 (
    .addr(CAR_output), .data({rom_1_data_4, rom_1_data_3, rom_1_data_2, rom_1_data}));  // open: sel
  Adder #(.width(9)) adder_1 (.a(CAR_output), .b(9'h1), .out(adder_1_out));  // open: cin, cout
  Hex_Digit_Display hex_digit_display_1 (.value(IR[15:12]));  // open: dp
  Hex_Digit_Display hex_digit_display_2 (.value(IR[11:8]));  // open: dp
  Clock CLK (.out(CLK_out));
  Hex_Digit_Display hex_digit_display_3 (.value(IR[7:4]));  // open: dp
  Hex_Digit_Display hex_digit_display_4 (.value(IR[3:0]));  // open: dp
  SBR SBR (.CLK(CLK_out), .Load(SBRLoad), .Input(adder_1_out), .Output(SBR_output));
  ROM #(.addrWidth(6), .dataWidth(21)) rom_2 (
    .addr(rom_1_data_4),
    .data({FunSelRF, MuxCSel, FunSelALU, MuxASel, MuxBSel, FunSelARF, OutDSel, Store, Load, L_H, En, FunSelIR}));  // open: sel
  proj2part2_main proj2 (
    .MuxCSel(MuxCSel), .OutASel(OutASel), .OutBSel(OutBSel), .RegSelRF(RegSelRF), .FunSelALU(FunSelALU),
    .FunSelRF(FunSelRF), .CLK(CLK_out), .MuxASel(MuxASel), .FunSelARF(FunSelARF), .RegSelARF(RegSelARF),
    .Store(Store), .L_H(L_H), .En(En), .FunSelIR(FunSelIR), .MuxBSel(MuxBSel), .OutCsel(OutCSel),
    .OutDsel(OutDSel), .Z(Z), .Load(Load), .Instruction(IR));
  MicropDecoder Decoder (
    .in_1(rom_1_data_4), .Out0(MOP0), .Out1(MOP1), .Out2(MOP2), .Out3(MOP3), .Out4(MOP4), .Out5(MOP5),
    .Out6(MOP6), .Out7(MOP7), .Out8(MOP8), .Out9(MOP9), .Out10(MOP10), .Out11(MOP11), .Out12(MOP12),
    .Out13(MOP13), .Out14(MOP14), .Out15(MOP15), .Out16(MOP16), .Out17(MOP17), .Out18(MOP18), .Out19(MOP19),
    .Out20(MOP20), .Out21(MOP21), .Out22(MOP22), .Out23(MOP23), .Out24(MOP24), .Out25(MOP25), .Out26(MOP26),
    .Out27(MOP27), .Out28(MOP28), .Out29(MOP29), .Out30(MOP30), .Out31(MOP31), .Out32(MOP32), .Out33(MOP33),
    .Out34(MOP34), .Out35(MOP35), .Out36(MOP36), .Out37(MOP37), .Out38(MOP38), .Out39(MOP39), .Out40(MOP40),
    .Out41(MOP41), .Out42(MOP42), .Out43(MOP43), .Out44(MOP44), .Out45(MOP45), .Out46(MOP46), .Out47(MOP47),
    .Out48(MOP48), .Out49(MOP49), .Out50(MOP50), .Out51(MOP51), .Out52(MOP52), .Out53(MOP53), .Out54(MOP54),
    .Out55(MOP55), .Out56(MOP56), .Out57(MOP57), .Out58(MOP58), .Out59(MOP59), .Out60(MOP60), .Out61(MOP61),
    .Out62(MOP62), .Out63(MOP63));
  or or_2 (or_2_out, MOP3, MOP9);
  assign OutASel = or_3_out ? IR[3:2] : 2'bz;  // Controlled_Buffer controlled_buffer_1
  or or_3 (or_3_out, MOP19, MOP21);
  assign OutASel = or_2_out ? IR[10:9] : 2'bz;  // Controlled_Buffer controlled_buffer_2
  assign OutASel = or_4_out ? IR[6:5] : 2'bz;  // Controlled_Buffer controlled_buffer_3
  or or_4 (or_4_out, MOP4, MOP7, MOP13, MOP16, MOP29, MOP32, MOP35, MOP41, MOP44, MOP46, MOP48, MOP50, MOP52, MOP54);
  assign OutASel = MOP24 ? IR[9:8] : 2'bz;  // Controlled_Buffer controlled_buffer_4
  or or_5 (or_5_out, MOP13, MOP15, MOP16, MOP18, MOP29, MOP31, MOP32, MOP34, MOP35, MOP40, MOP41, MOP43);
  or or_6 (or_6_out, MOP14, MOP17, MOP19, MOP20, MOP21, MOP22, MOP30, MOP33, MOP39, MOP42);
  assign OutBSel = or_5_out ? IR[3:2] : 2'bz;  // Controlled_Buffer controlled_buffer_5
  assign OutBSel = or_6_out ? IR[6:5] : 2'bz;  // Controlled_Buffer controlled_buffer_6
  or or_7 (or_7_out, MOP1, MOP2, MOP12);
  RFDecoder RFDecoder (.Input(IR[9:8]), .Output(RFDecoder_output));
  or or_8 (or_8_out, MOP4, MOP5, MOP13, MOP14, MOP15, MOP19, MOP20, MOP23, MOP27, MOP29, MOP30, MOP31, MOP35, MOP39, MOP40, MOP44, MOP45, MOP48, MOP49, MOP52, MOP53);
  RFDecoder RFDecoder_2 (.Input(IR[10:9]), .Output(RFDecoder_2_output));
  assign RegSelRF = or_7_out ? RFDecoder_2_output : 4'bz;  // Controlled_Buffer controlled_buffer_7
  assign RegSelRF = or_8_out ? RFDecoder_output : 4'bz;  // Controlled_Buffer controlled_buffer_8
  or or_9 (or_9_out, MOP56, MOP58, MOP60);
  or or_10 (or_10_out, MOP10, MOP11);
  ARFDecoder ARFDecoder (.Input(IR[9:8]), .Output(ARFDecoder_output));
  assign RegSelARF = or_9_out ? 3'b001 : 3'bz;  // Controlled_Buffer controlled_buffer_9
  assign RegSelARF = or_10_out ? 3'b010 : 3'bz;  // Controlled_Buffer controlled_buffer_10
  assign RegSelARF = or_11_out ? ARFDecoder_output : 3'bz;  // Controlled_Buffer controlled_buffer_11
  or or_11 (or_11_out, MOP7, MOP8, MOP16, MOP17, MOP18, MOP21, MOP22, MOP25, MOP28, MOP32, MOP33, MOP34, MOP41, MOP42, MOP43, MOP46, MOP47, MOP50, MOP51, MOP54, MOP55);
  OutConverter OutConverter (.Input(IR[3:2]), .Output(OutConverter_output));
  or or_12 (or_12_out, MOP14, MOP17, MOP20, MOP30, MOP33, MOP39, MOP42);
  OutConverter OutConverter_2 (.Input(IR[6:5]), .Output(OutConverter_2_output));
  or or_13 (or_13_out, MOP5, MOP8, MOP15, MOP18, MOP31, MOP34, MOP40, MOP43, MOP45, MOP47, MOP49, MOP51, MOP53, MOP55);
  OutConverter OutConverter_3 (.Input(IR[9:8]), .Output(OutConverter_3_output));
  assign OutCSel = or_12_out ? OutConverter_output : 2'bz;  // Controlled_Buffer controlled_buffer_12
  assign OutCSel = or_13_out ? OutConverter_2_output : 2'bz;  // Controlled_Buffer controlled_buffer_13
  assign OutCSel = MOP26 ? OutConverter_3_output : 2'bz;  // Controlled_Buffer controlled_buffer_14
  assign OutCSel = MOP57 ? 2'b00 : 2'bz;  // Controlled_Buffer controlled_buffer_15

  // Notes on the sheet:
  //   CD
  //   Branch Address
  //   BR
  //   Branch Logic
  //   Microprograms
  //   contents of rom_1 (hex, n*v repeats v):
  //   76001 78002 7a003 78600 70400 251*0 2000 0 0 0 4000 0 0 0 6000 0 0 0 8000 0 0 0 a000 0 0 0 e000 0 0
  //   0 10000 0 0 0 1211d 14000 0 0 16121 18000 0 0 1a000 0 0 0 1c000 0 0 0 1e000 0 0 0 20000 0 0 0 22000
  //   0 0 0 24000 0 0 0 26000 0 0 0 28000 0 0 0 2a000 0 0 0 2c000 0 0 0 814d 2e14e 30000 0 a151 2e152
  //   30000 0 e155 32156 34000 0 10159 3215a 34000 0 815d 3615e 30000 0 a161 36162 30000 0 e165 38166
  //   34000 0 10169 3816a 34000 0 3a000 0 0 0 3c000 0 0 0 3e000 0 0 0 40000 0 0 0 42000 0 0 0 44000 0 0 0
  //   46000 0 0 0 4e000 0 0 0 50000 0 0 0 52000 0 0 0 54000 0 0 0 56000 0 0 0 58000 0 0 0 5a000 0 0 0
  //   5c000 0 0 0 5e000 0 0 0 60000 0 0 0 62000 0 0 0 64000 0 0 0 66000 0 0 0 68000 0 0 0 6a000 0 0 0
  //   6c000 0 0 0 6e000 0 0 0 204 0 0 0 a04 0 0 0 1204 0 0 0 721d9 14204 0 0 161dd 74000
  //   ROM1
  //   Incrementer
  //   Microoperations
  //   ROM2
  //   contents of rom_2 (hex, n*v repeats v):
  //   0 81050 80000 40060 83000 82000 0 40d00 2d00 400a0 300 200 81090 d3000 93000 93000 50d00 10d00 10d00
  //   db000 9b000 58d00 18d00 180000 40000 300 0 100000 200 df000 9f000 9f000 5cd00 1cd00 1cd00 e3000 0 0
  //   0 a3000 a3000 60d00 20d00 20d00 cb000 8b000 48100 8d00 eb000 ab000 68d00 28d00 ef000 af000 6cd00
  //   2cd00 500 a0 990 1f 200 17
  //   Instruction
  //   Control Signals
endmodule

module CAR (
  input  CLK,
  input  [8:0] Input,
  output [8:0] Output
);

  D_Flip_Flop d_ff_1 (.clk(CLK), .D(Input[0]), .Q(Output[0]));  // open: Qn, preset, en, reset
  D_Flip_Flop d_ff_2 (.clk(CLK), .D(Input[1]), .Q(Output[1]));  // open: Qn, preset, en, reset
  D_Flip_Flop d_ff_3 (.clk(CLK), .D(Input[2]), .Q(Output[2]));  // open: Qn, preset, en, reset
  D_Flip_Flop d_ff_4 (.clk(CLK), .D(Input[3]), .Q(Output[3]));  // open: Qn, preset, en, reset
  D_Flip_Flop d_ff_5 (.clk(CLK), .D(Input[4]), .Q(Output[4]));  // open: Qn, preset, en, reset
  D_Flip_Flop d_ff_6 (.clk(CLK), .D(Input[5]), .Q(Output[5]));  // open: Qn, preset, en, reset
  D_Flip_Flop d_ff_7 (.clk(CLK), .D(Input[6]), .Q(Output[6]));  // open: Qn, preset, en, reset
  D_Flip_Flop d_ff_8 (.clk(CLK), .D(Input[7]), .Q(Output[7]));  // open: Qn, preset, en, reset
  D_Flip_Flop d_ff_9 (.clk(CLK), .D(Input[8]), .Q(Output[8]));  // open: Qn, preset, en, reset
endmodule

module SBR (
  input  CLK,
  input  Load,
  input  [8:0] Input,
  output [8:0] Output
);

  D_Flip_Flop d_ff_1 (.clk(CLK), .D(Input[0]), .Q(Output[0]), .en(Load));  // open: Qn, preset, reset
  D_Flip_Flop d_ff_2 (.clk(CLK), .D(Input[1]), .Q(Output[1]), .en(Load));  // open: Qn, preset, reset
  D_Flip_Flop d_ff_3 (.clk(CLK), .D(Input[2]), .Q(Output[2]), .en(Load));  // open: Qn, preset, reset
  D_Flip_Flop d_ff_4 (.clk(CLK), .D(Input[3]), .Q(Output[3]), .en(Load));  // open: Qn, preset, reset
  D_Flip_Flop d_ff_5 (.clk(CLK), .D(Input[4]), .Q(Output[4]), .en(Load));  // open: Qn, preset, reset
  D_Flip_Flop d_ff_6 (.clk(CLK), .D(Input[5]), .Q(Output[5]), .en(Load));  // open: Qn, preset, reset
  D_Flip_Flop d_ff_7 (.clk(CLK), .D(Input[6]), .Q(Output[6]), .en(Load));  // open: Qn, preset, reset
  D_Flip_Flop d_ff_8 (.clk(CLK), .D(Input[7]), .Q(Output[7]), .en(Load));  // open: Qn, preset, reset
  D_Flip_Flop d_ff_9 (.clk(CLK), .D(Input[8]), .Q(Output[8]), .en(Load));  // open: Qn, preset, reset
endmodule

module MAP (
  input  [15:0] IR,
  output [8:0] Output
);

  wire ADD, AND, and_1_out, and_2_out, and_3_out, and_4_out, and_5_out, and_6_out, and_7_out, and_8_out,
       and_9_out, and_10_out, and_11_out, and_12_out, and_13_out, and_14_out, and_15_out, and_16_out,
       and_17_out, and_18_out, and_19_out, and_20_out, and_21_out, and_22_out, and_23_out, and_24_out,
       and_25_out, and_26_out, and_27_out, and_28_out, and_29_out, and_30_out, and_31_out, and_32_out,
       and_33_out, and_34_out, and_35_out, and_36_out, and_37_out, and_38_out, and_39_out, and_40_out,
       and_41_out, and_42_out, and_43_out, and_44_out, and_45_out, and_46_out, and_47_out, and_48_out, BEQ,
       BNE, BRA, CALL, DEC, INC, LD, LSL, LSR, MOV, NOT, not_1_out, not_2_out, not_3_out, not_4_out,
       not_5_out, not_6_out, not_7_out, not_8_out, not_9_out, not_10_out, not_11_out, not_12_out, not_13_out,
       not_14_out, not_15_out, not_16_out, not_17_out, not_18_out, not_19_out, not_20_out, not_21_out,
       not_22_out, not_23_out, not_24_out, not_25_out, OR, PSH, PUL, RET, ST, SUB;

  Decoder #(.select(5)) decoder_1 (
    .out0(LD), .out1(ST), .out2(MOV), .out3(PSH), .out4(PUL), .out5(ADD), .out6(SUB), .out7(DEC), .out8(INC),
    .out9(AND), .out10(OR), .out11(NOT), .out12(LSL), .out13(LSR), .out14(BRA), .out15(BEQ), .out16(BNE),
    .out17(CALL), .out18(RET), .sel(IR[15:11]));  // open: out19, out20, out21, out22, out23, out24, out25, out26, out27, out28, out29, out30, out31, en
  not not_1 (not_1_out, IR[8]);
  and and_1 (and_1_out, LD, IR[8]);
  and and_2 (and_2_out, LD, not_1_out);
  not not_2 (not_2_out, IR[7]);
  not not_3 (not_3_out, IR[10]);
  assign Output[7:2] = and_1_out ? {6{1'b0}} : 6'bz;  // Controlled_Buffer controlled_buffer_1
  assign Output[7:2] = and_2_out ? 6'b000001 : 6'bz;  // Controlled_Buffer controlled_buffer_2
  assign Output[7:2] = ST ? 6'b000010 : 6'bz;  // Controlled_Buffer controlled_buffer_3
  assign Output[7:2] = PSH ? 6'b000111 : 6'bz;  // Controlled_Buffer controlled_buffer_4
  assign Output[7:2] = PUL ? 6'b001000 : 6'bz;  // Controlled_Buffer controlled_buffer_5
  and and_3 (and_3_out, MOV, not_2_out, not_3_out);
  assign Output[7:2] = and_3_out ? 6'b000011 : 6'bz;  // Controlled_Buffer controlled_buffer_6
  and and_4 (and_4_out, MOV, IR[7], not_3_out);
  assign Output[7:2] = and_4_out ? 6'b000100 : 6'bz;  // Controlled_Buffer controlled_buffer_7
  and and_5 (and_5_out, MOV, not_2_out, IR[10]);
  assign Output[7:2] = and_5_out ? 6'b000101 : 6'bz;  // Controlled_Buffer controlled_buffer_8
  and and_6 (and_6_out, MOV, IR[7], IR[10]);
  assign Output[7:2] = and_6_out ? 6'b000110 : 6'bz;  // Controlled_Buffer controlled_buffer_9
  not not_4 (not_4_out, IR[4]);
  not not_5 (not_5_out, IR[7]);
  not not_6 (not_6_out, IR[10]);
  not not_7 (not_7_out, IR[4]);
  not not_8 (not_8_out, IR[7]);
  not not_9 (not_9_out, IR[10]);
  and and_7 (and_7_out, ADD, not_4_out, not_5_out, not_6_out);
  assign Output[7:2] = and_7_out ? 6'b001001 : 6'bz;  // Controlled_Buffer controlled_buffer_10
  and and_8 (and_8_out, ADD, IR[4], not_5_out, not_6_out);
  assign Output[7:2] = and_8_out ? 6'b001010 : 6'bz;  // Controlled_Buffer controlled_buffer_11
  and and_9 (and_9_out, ADD, not_4_out, IR[7], not_6_out);
  assign Output[7:2] = and_9_out ? 6'b001011 : 6'bz;  // Controlled_Buffer controlled_buffer_12
  and and_10 (and_10_out, ADD, not_4_out, not_5_out, IR[10]);
  assign Output[7:2] = and_10_out ? 6'b001100 : 6'bz;  // Controlled_Buffer controlled_buffer_13
  and and_11 (and_11_out, ADD, IR[4], not_5_out, IR[10]);
  assign Output[7:2] = and_11_out ? 6'b001101 : 6'bz;  // Controlled_Buffer controlled_buffer_14
  and and_12 (and_12_out, ADD, not_4_out, IR[7], IR[10]);
  assign Output[7:2] = and_12_out ? 6'b001110 : 6'bz;  // Controlled_Buffer controlled_buffer_15
  and and_13 (and_13_out, SUB, not_7_out, not_8_out, not_9_out);
  and and_14 (and_14_out, SUB, IR[4], not_8_out, not_9_out);
  and and_15 (and_15_out, SUB, not_7_out, not_8_out, IR[10]);
  and and_16 (and_16_out, SUB, IR[4], not_8_out, IR[10]);
  assign Output[7:2] = and_13_out ? 6'b001111 : 6'bz;  // Controlled_Buffer controlled_buffer_16
  assign Output[7:2] = and_14_out ? 6'b010000 : 6'bz;  // Controlled_Buffer controlled_buffer_17
  assign Output[7:2] = and_15_out ? 6'b010001 : 6'bz;  // Controlled_Buffer controlled_buffer_18
  assign Output[7:2] = and_16_out ? 6'b010010 : 6'bz;  // Controlled_Buffer controlled_buffer_19
  not not_10 (not_10_out, IR[7]);
  not not_11 (not_11_out, IR[10]);
  not not_12 (not_12_out, IR[7]);
  not not_13 (not_13_out, IR[10]);
  and and_17 (and_17_out, DEC, not_10_out, not_11_out);
  assign Output[7:2] = and_17_out ? 6'b010011 : 6'bz;  // Controlled_Buffer controlled_buffer_20
  and and_18 (and_18_out, DEC, IR[7], not_11_out);
  assign Output[7:2] = and_18_out ? 6'b010100 : 6'bz;  // Controlled_Buffer controlled_buffer_21
  and and_19 (and_19_out, DEC, not_10_out, IR[10]);
  assign Output[7:2] = and_19_out ? 6'b010101 : 6'bz;  // Controlled_Buffer controlled_buffer_22
  and and_20 (and_20_out, DEC, IR[7], IR[10]);
  assign Output[7:2] = and_20_out ? 6'b010110 : 6'bz;  // Controlled_Buffer controlled_buffer_23
  and and_21 (and_21_out, INC, not_12_out, not_13_out);
  assign Output[7:2] = and_21_out ? 6'b010111 : 6'bz;  // Controlled_Buffer controlled_buffer_24
  and and_22 (and_22_out, INC, IR[7], not_13_out);
  assign Output[7:2] = and_22_out ? 6'b011000 : 6'bz;  // Controlled_Buffer controlled_buffer_25
  and and_23 (and_23_out, INC, not_12_out, IR[10]);
  assign Output[7:2] = and_23_out ? 6'b011001 : 6'bz;  // Controlled_Buffer controlled_buffer_26
  and and_24 (and_24_out, INC, IR[7], IR[10]);
  assign Output[7:2] = and_24_out ? 6'b011010 : 6'bz;  // Controlled_Buffer controlled_buffer_27
  not not_14 (not_14_out, IR[4]);
  not not_15 (not_15_out, IR[7]);
  not not_16 (not_16_out, IR[10]);
  not not_17 (not_17_out, IR[4]);
  not not_18 (not_18_out, IR[7]);
  not not_19 (not_19_out, IR[10]);
  and and_25 (and_25_out, AND, not_14_out, not_15_out, not_16_out);
  and and_26 (and_26_out, AND, IR[4], not_15_out, not_16_out);
  and and_27 (and_27_out, AND, not_14_out, IR[7], not_16_out);
  and and_28 (and_28_out, AND, not_14_out, not_15_out, IR[10]);
  and and_29 (and_29_out, AND, IR[4], not_15_out, IR[10]);
  and and_30 (and_30_out, AND, not_14_out, IR[7], IR[10]);
  assign Output[7:2] = and_25_out ? 6'b011011 : 6'bz;  // Controlled_Buffer controlled_buffer_28
  assign Output[7:2] = and_26_out ? 6'b011100 : 6'bz;  // Controlled_Buffer controlled_buffer_29
  assign Output[7:2] = and_27_out ? 6'b011101 : 6'bz;  // Controlled_Buffer controlled_buffer_30
  assign Output[7:2] = and_28_out ? 6'b011110 : 6'bz;  // Controlled_Buffer controlled_buffer_31
  assign Output[7:2] = and_29_out ? 6'b011111 : 6'bz;  // Controlled_Buffer controlled_buffer_32
  assign Output[7:2] = and_30_out ? 6'b100000 : 6'bz;  // Controlled_Buffer controlled_buffer_33
  and and_31 (and_31_out, OR, not_17_out, not_18_out, not_19_out);
  assign Output[7:2] = and_31_out ? 6'b100001 : 6'bz;  // Controlled_Buffer controlled_buffer_34
  and and_32 (and_32_out, OR, IR[4], not_18_out, not_19_out);
  assign Output[7:2] = and_32_out ? 6'b100010 : 6'bz;  // Controlled_Buffer controlled_buffer_35
  and and_33 (and_33_out, OR, not_17_out, IR[7], not_19_out);
  assign Output[7:2] = and_33_out ? 6'b100011 : 6'bz;  // Controlled_Buffer controlled_buffer_36
  and and_34 (and_34_out, OR, not_17_out, not_18_out, IR[10]);
  assign Output[7:2] = and_34_out ? 6'b100100 : 6'bz;  // Controlled_Buffer controlled_buffer_37
  and and_35 (and_35_out, OR, IR[4], not_18_out, IR[10]);
  assign Output[7:2] = and_35_out ? 6'b100101 : 6'bz;  // Controlled_Buffer controlled_buffer_38
  and and_36 (and_36_out, OR, not_17_out, IR[7], IR[10]);
  assign Output[7:2] = and_36_out ? 6'b100110 : 6'bz;  // Controlled_Buffer controlled_buffer_39
  not not_20 (not_20_out, IR[7]);
  and and_37 (and_37_out, NOT, not_20_out, not_21_out);
  not not_21 (not_21_out, IR[10]);
  and and_38 (and_38_out, NOT, IR[7], not_21_out);
  and and_39 (and_39_out, NOT, not_20_out, IR[10]);
  and and_40 (and_40_out, NOT, IR[7], IR[10]);
  not not_22 (not_22_out, IR[7]);
  not not_23 (not_23_out, IR[10]);
  assign Output[7:2] = and_37_out ? 6'b100111 : 6'bz;  // Controlled_Buffer controlled_buffer_40
  assign Output[7:2] = and_38_out ? 6'b101000 : 6'bz;  // Controlled_Buffer controlled_buffer_41
  assign Output[7:2] = and_39_out ? 6'b101001 : 6'bz;  // Controlled_Buffer controlled_buffer_42
  assign Output[7:2] = and_40_out ? 6'b101010 : 6'bz;  // Controlled_Buffer controlled_buffer_43
  and and_41 (and_41_out, LSL, not_22_out, not_23_out);
  assign Output[7:2] = and_41_out ? 6'b101011 : 6'bz;  // Controlled_Buffer controlled_buffer_44
  and and_42 (and_42_out, LSL, IR[7], not_23_out);
  assign Output[7:2] = and_42_out ? 6'b101100 : 6'bz;  // Controlled_Buffer controlled_buffer_45
  and and_43 (and_43_out, LSL, not_22_out, IR[10]);
  assign Output[7:2] = and_43_out ? 6'b101101 : 6'bz;  // Controlled_Buffer controlled_buffer_46
  and and_44 (and_44_out, LSL, IR[7], IR[10]);
  assign Output[7:2] = and_44_out ? 6'b101110 : 6'bz;  // Controlled_Buffer controlled_buffer_47
  not not_24 (not_24_out, IR[7]);
  not not_25 (not_25_out, IR[10]);
  and and_45 (and_45_out, LSR, not_24_out, not_25_out);
  assign Output[7:2] = and_45_out ? 6'b101111 : 6'bz;  // Controlled_Buffer controlled_buffer_48
  and and_46 (and_46_out, LSR, IR[7], not_25_out);
  assign Output[7:2] = and_46_out ? 6'b110000 : 6'bz;  // Controlled_Buffer controlled_buffer_49
  and and_47 (and_47_out, LSR, not_24_out, IR[10]);
  assign Output[7:2] = and_47_out ? 6'b110001 : 6'bz;  // Controlled_Buffer controlled_buffer_50
  and and_48 (and_48_out, LSR, IR[7], IR[10]);
  assign Output[7:2] = and_48_out ? 6'b110010 : 6'bz;  // Controlled_Buffer controlled_buffer_51
  assign Output[7:2] = BRA ? 6'b110011 : 6'bz;  // Controlled_Buffer controlled_buffer_52
  assign Output[7:2] = BEQ ? 6'b110100 : 6'bz;  // Controlled_Buffer controlled_buffer_53
  assign Output[7:2] = BNE ? 6'b110101 : 6'bz;  // Controlled_Buffer controlled_buffer_54
  assign Output[7:2] = CALL ? 6'b110110 : 6'bz;  // Controlled_Buffer controlled_buffer_55
  assign Output[7:2] = RET ? 6'b110111 : 6'bz;  // Controlled_Buffer controlled_buffer_56

  assign {Output[8], Output[1:0]} = 3'b100;

  // Other names for the same wires on the sheet: ROUTINE[5:0] = Output[7:2]
endmodule

module RFDecoder (
  input  [1:0] Input,
  output [3:0] Output
);

  Multiplexer #(.select(2), .width(4)) multiplexer_1 (
    .in0(4'b0001), .in1(4'b0010), .in2(4'b0100), .in3(4'b1000), .out(Output), .sel(Input));  // open: en
endmodule

module ARFDecoder (
  input  [1:0] Input,
  output [2:0] Output
);

  Multiplexer #(.select(2), .width(3)) multiplexer_1 (
    .in0(3'b001), .in1(3'b001), .in2(3'b010), .in3(3'b100), .out(Output), .sel(Input));  // open: en
endmodule

module OutConverter (
  input  [1:0] Input,
  output [1:0] Output
);

  Multiplexer #(.select(2), .width(2)) multiplexer_1 (
    .in0(2'b00), .in1(2'b00), .in2(2'b01), .in3(2'b10), .out(Output), .sel(Input));  // open: en
endmodule

module MicropDecoder (
  input  [5:0] in_1,
  output Out0,
  output Out1,
  output Out2,
  output Out3,
  output Out4,
  output Out5,
  output Out6,
  output Out7,
  output Out8,
  output Out9,
  output Out10,
  output Out11,
  output Out12,
  output Out13,
  output Out14,
  output Out15,
  output Out16,
  output Out17,
  output Out18,
  output Out19,
  output Out20,
  output Out21,
  output Out22,
  output Out23,
  output Out24,
  output Out25,
  output Out26,
  output Out27,
  output Out28,
  output Out29,
  output Out30,
  output Out31,
  output Out32,
  output Out33,
  output Out34,
  output Out35,
  output Out36,
  output Out37,
  output Out38,
  output Out39,
  output Out40,
  output Out41,
  output Out42,
  output Out43,
  output Out44,
  output Out45,
  output Out46,
  output Out47,
  output Out48,
  output Out49,
  output Out50,
  output Out51,
  output Out52,
  output Out53,
  output Out54,
  output Out55,
  output Out56,
  output Out57,
  output Out58,
  output Out59,
  output Out60,
  output Out61,
  output Out62,
  output Out63
);

  wire decoder_1_out0, decoder_1_out1;

  Decoder #(.disabled(0), .enable("false")) decoder_1 (.out0(decoder_1_out0), .out1(decoder_1_out1), .sel(in_1[5]));
  Decoder #(.select(5), .disabled(0)) decoder_2 (
    .out0(Out0), .out1(Out1), .out2(Out2), .out3(Out3), .out4(Out4), .out5(Out5), .out6(Out6), .out7(Out7),
    .out8(Out8), .out9(Out9), .out10(Out10), .out11(Out11), .out12(Out12), .out13(Out13), .out14(Out14),
    .out15(Out15), .out16(Out16), .out17(Out17), .out18(Out18), .out19(Out19), .out20(Out20), .out21(Out21),
    .out22(Out22), .out23(Out23), .out24(Out24), .out25(Out25), .out26(Out26), .out27(Out27), .out28(Out28),
    .out29(Out29), .out30(Out30), .out31(Out31), .sel(in_1[4:0]), .en(decoder_1_out0));
  Decoder #(.select(5), .disabled(0)) decoder_3 (
    .out0(Out32), .out1(Out33), .out2(Out34), .out3(Out35), .out4(Out36), .out5(Out37), .out6(Out38),
    .out7(Out39), .out8(Out40), .out9(Out41), .out10(Out42), .out11(Out43), .out12(Out44), .out13(Out45),
    .out14(Out46), .out15(Out47), .out16(Out48), .out17(Out49), .out18(Out50), .out19(Out51), .out20(Out52),
    .out21(Out53), .out22(Out54), .out23(Out55), .out24(Out56), .out25(Out57), .out26(Out58), .out27(Out59),
    .out28(Out60), .out29(Out61), .out30(Out62), .out31(Out63), .sel(in_1[4:0]), .en(decoder_1_out1));
endmodule
